# Fritzing sketch Z80 Breadboard Computer #1.0 (saved by Fritzing 0.9.4)
breadboards: 1

parts:
  IC1 = Z80 A [package="DIP (Dual Inline) [THT]"]
  LED2 = LED - 5mm [color="Red (633nm)" package="5 mm [THT]"]
  LED3 = LED - 5mm [color="Red (633nm)" package="5 mm [THT]"]
  LED4 = LED - 5mm [color="Red (633nm)" package="5 mm [THT]"]
  LED5 = LED - 5mm [color="Red (633nm)" package="5 mm [THT]"]
  LED6 = LED - 5mm [color="Red (633nm)" package="5 mm [THT]"]
  LED7 = LED - 5mm [color="Red (633nm)" package="5 mm [THT]"]
  LED8 = LED - 5mm [color="Red (633nm)" package="5 mm [THT]"]
  R1 = Resistor [tolerance=±5% resistance=470 package=THT]
  R2 = Resistor [tolerance=±5% resistance=470 package=THT]
  R3 = Resistor [tolerance=±5% resistance=470 package=THT]
  R4 = Resistor [tolerance=±5% resistance=470 package=THT]
  R5 = Resistor [tolerance=±5% resistance=470 package=THT]
  R6 = Resistor [tolerance=±5% resistance=470 package=THT]
  R7 = Resistor [tolerance=±5% resistance=470 package=THT]
  R8 = Resistor [tolerance=±5% resistance=470 package=THT]
  R9 = Resistor [tolerance=±5% resistance=470 package=THT]
  R10 = Resistor [tolerance=±5% resistance=470 package=THT]
  R11 = Resistor [tolerance=±5% resistance=470 package=THT]
  R12 = Resistor [tolerance=±5% resistance=470 package=THT]
  R13 = Resistor [tolerance=±5% resistance=470 package=THT]
  R14 = Resistor [tolerance=±5% resistance=470 package=THT]
  R15 = Resistor [tolerance=±5% resistance=470 package=THT]
  R16 = Resistor [tolerance=±5% resistance=470 package=THT]
  C1 = Ceramic Capacitor [capacitance=0.1µF package="100 mil [THT, multilayer]"]
  LED1 = LED - 5mm [color="Red (633nm)" package="5 mm [THT]"]
  S1 = Pushbutton [package="[THT]"]
  R17 = Resistor [tolerance=±5% resistance=470 package=THT]
  C2 = Ceramic Capacitor [capacitance=10nF package="100 mil [THT, multilayer]"]
  R19 = Resistor [tolerance=±5% resistance=1k package=THT]
  R20 = Resistor [tolerance=±5% resistance=3.3k package=THT]
  U1 = 555 Timer [package="DIP8 [THT]"]
  R18 = Rotary Potentiometer (Small) [maximum_resistance=10kΩ package=THT]
  LED9 = LED - 5mm [color="Green (560nm)" package="5 mm [THT]"]
  R21 = Resistor [tolerance=±5% resistance=470 package=THT]
  C3 = Electrolytic Capacitor [capacitance=10µF package="100 mil [THT, electrolytic]"]
  C4 = Electrolytic Capacitor [capacitance=10µF package="100 mil [THT, electrolytic]"]

nets:
  CLOCK: IC1.CLK, U1.Output, LED9.anode
  N1: IC1.D4, R13.Pin_1
  N2: IC1.D3, R12.Pin_1
  N3: IC1.D5, R14.Pin_1
  N4: IC1.D6, R15.Pin_1
  5V: IC1.+5V, IC1.!_INT, IC1.!_NMI, IC1.!_WAIT, IC1.!_BUSRQ, C1.1, R17.Pin_0, R19.Pin_1, U1.Reset, U1.Vcc_Supply_Voltage, C4.+
  N5: IC1.D2, R11.Pin_1
  N6: IC1.D7, R16.Pin_1
  N7: IC1.D0, R9.Pin_1
  N8: IC1.D1, R10.Pin_1
  N9: IC1.!_RESET, S1.Pin_3, S1.Pin_4, R17.Pin_1
  GND: IC1.GND, R1.Pin_1, R2.Pin_1, R3.Pin_1, R4.Pin_1, R5.Pin_1, R6.Pin_1, R7.Pin_1, R8.Pin_1, R9.Pin_0, R10.Pin_0, R11.Pin_0, R12.Pin_0, R13.Pin_0, R14.Pin_0, R15.Pin_0, R16.Pin_0, C1.0, S1.Pin_1, S1.Pin_2, C2.1, U1.Ground, R21.Pin_0, C3.-, C4.-
  N10: IC1.A0, LED1.anode
  N11: IC1.A1, LED2.anode
  N12: IC1.A2, LED3.anode
  N13: IC1.A3, LED4.anode
  N14: IC1.A4, LED5.anode
  N15: IC1.A5, LED6.anode
  N16: IC1.A6, LED7.anode
  N17: IC1.A7, LED8.anode
  N18: LED2.cathode, R2.Pin_0
  N19: LED3.cathode, R3.Pin_0
  N20: LED4.cathode, R4.Pin_0
  N21: LED5.cathode, R5.Pin_0
  N22: LED6.cathode, R6.Pin_0
  N23: LED7.cathode, R7.Pin_0
  N24: LED8.cathode, R8.Pin_0
  N25: R1.Pin_0, LED1.cathode
  N26: C2.0, U1.Control_Voltage
  N27: R19.Pin_0, R20.Pin_1, U1.Discharge
  N28: R20.Pin_0, R18.leg2
  N29: U1.Trigger, U1.Threshold, R18.wiper, C3.+
  N30: LED9.cathode, R21.Pin_1

custom parts:
  Z80 A: Zilog Z80 A CPU
