# Fritzing sketch Z80 Breadboard Computer #3.0 (saved by Fritzing 0.9.4)
breadboards: 3

parts:
  IC1 = Z80 A [package="DIP (Dual Inline) [THT]"]
  LED2 = LED - 5mm [color="Red (633nm)" package="5 mm [THT]"]
  LED3 = LED - 5mm [color="Red (633nm)" package="5 mm [THT]"]
  LED4 = LED - 5mm [color="Red (633nm)" package="5 mm [THT]"]
  LED5 = LED - 5mm [color="Red (633nm)" package="5 mm [THT]"]
  LED6 = LED - 5mm [color="Red (633nm)" package="5 mm [THT]"]
  LED7 = LED - 5mm [color="Red (633nm)" package="5 mm [THT]"]
  LED8 = LED - 5mm [color="Red (633nm)" package="5 mm [THT]"]
  R1 = Resistor [tolerance=±5% resistance=470 package=THT]
  R2 = Resistor [tolerance=±5% resistance=470 package=THT]
  R3 = Resistor [tolerance=±5% resistance=470 package=THT]
  R4 = Resistor [tolerance=±5% resistance=470 package=THT]
  R5 = Resistor [tolerance=±5% resistance=470 package=THT]
  R6 = Resistor [tolerance=±5% resistance=470 package=THT]
  R7 = Resistor [tolerance=±5% resistance=470 package=THT]
  R8 = Resistor [tolerance=±5% resistance=470 package=THT]
  C1 = Ceramic Capacitor [capacitance=0.1µF package="100 mil [THT, multilayer]"]
  LED1 = LED - 5mm [color="Red (633nm)" package="5 mm [THT]"]
  S1 = Pushbutton [package="[THT]"]
  R17 = Resistor [tolerance=±5% resistance=470 package=THT]
  C2 = Ceramic Capacitor [capacitance=10nF package="100 mil [THT, multilayer]"]
  R19 = Resistor [tolerance=±5% resistance=1k package=THT]
  R20 = Resistor [tolerance=±5% resistance=3.3k package=THT]
  U1 = 555 Timer [package="DIP8 [THT]"]
  R18 = Rotary Potentiometer (Small) [maximum_resistance=10kΩ package=THT]
  LED9 = LED - 5mm [color="Green (560nm)" package="5 mm [THT]"]
  R21 = Resistor [tolerance=±5% resistance=470 package=THT]
  C3 = Electrolytic Capacitor [capacitance=10µF package="100 mil [THT, electrolytic]"]
  C4 = Electrolytic Capacitor [capacitance=10µF package="100 mil [THT, electrolytic]"]
  IC2 = W27C512 [package="DIP (Dual Inline) [THT]"]
  C5 = Ceramic Capacitor [capacitance=0.1µF package="100 mil [THT, multilayer]"]
  IC3 = 628128 [package="DIP (Dual Inline) [THT]"]
  C6 = Ceramic Capacitor [capacitance=0.1µF package="100 mil [THT, multilayer]"]
  74HC139N1 = 74HC139N [part_number=74HC139N package="DIP (Dual Inline) [THT]"]

nets:
  A11: IC1.A11, IC2.A11, IC3.A11
  A12: IC1.A12, IC2.A12, IC3.A12
  A13: IC1.A13, IC2.A13, IC3.A13
  A14: IC1.A14, IC2.A14, IC3.A14
  A15: IC1.A15, IC2.A15, IC3.A15, 74HC139N1.1A
  CLOCK: IC1.CLK, U1.Output, LED9.anode
  D4: IC1.D4, IC2.Q4, IC3.D4
  D3: IC1.D3, IC2.Q3, IC3.D3
  D5: IC1.D5, IC2.Q5, IC3.D5
  D6: IC1.D6, IC2.Q6, IC3.D6
  5V: IC1.+5V, IC1.!_INT, IC1.!_NMI, IC1.!_WAIT, IC1.!_BUSRQ, C1.1, R17.Pin_0, R19.Pin_1, U1.Reset, U1.Vcc_Supply_Voltage, C4.+, IC2.Vcc, C5.1, IC3.Vcc, C6.1, 74HC139N1.VCC
  D2: IC1.D2, IC2.Q2, IC3.D2
  D7: IC1.D7, IC2.Q7, IC3.D7
  D0: IC1.D0, IC2.Q0, IC3.D0
  D1: IC1.D1, IC2.Q1, IC3.D1
  MREQ: IC1.!_MREQ, 74HC139N1.1G_
  RD: IC1.!_RD, IC2.OE/Vpp, IC3.OE
  WR: IC1.!_WR, IC3.WE
  N1: IC1.!_RESET, S1.Pin_3, S1.Pin_4, R17.Pin_1
  GND: IC1.GND, R1.Pin_1, R2.Pin_1, R3.Pin_1, R4.Pin_1, R5.Pin_1, R6.Pin_1, R7.Pin_1, R8.Pin_1, C1.0, S1.Pin_1, S1.Pin_2, C2.1, U1.Ground, R21.Pin_0, C3.-, C4.-, IC2.GND, C5.0, IC3.A16, IC3.Vss, IC3.CS1, C6.0, 74HC139N1.GND
  A0: IC1.A0, LED1.anode, IC2.A0, IC3.A0
  A1: IC1.A1, LED2.anode, IC2.A1, IC3.A1
  A2: IC1.A2, LED3.anode, IC2.A2, IC3.A2
  A3: IC1.A3, LED4.anode, IC2.A3, IC3.A3
  A4: IC1.A4, LED5.anode, IC2.A4, IC3.A4
  A5: IC1.A5, LED6.anode, IC2.A5, IC3.A5
  A6: IC1.A6, LED7.anode, IC2.A6, IC3.A6
  A7: IC1.A7, LED8.anode, IC2.A7, IC3.A7
  A8: IC1.A8, IC2.A8, IC3.A8
  A9: IC1.A9, IC2.A9, IC3.A9
  A10: IC1.A10, IC2.A10, IC3.A10
  N2: LED2.cathode, R2.Pin_0
  N3: LED3.cathode, R3.Pin_0
  N4: LED4.cathode, R4.Pin_0
  N5: LED5.cathode, R5.Pin_0
  N6: LED6.cathode, R6.Pin_0
  N7: LED7.cathode, R7.Pin_0
  N8: LED8.cathode, R8.Pin_0
  N9: R1.Pin_0, LED1.cathode
  N10: C2.0, U1.Control_Voltage
  N11: R19.Pin_0, R20.Pin_1, U1.Discharge
  N12: R20.Pin_0, R18.leg2
  N13: U1.Trigger, U1.Threshold, R18.wiper, C3.+
  N14: LED9.cathode, R21.Pin_1
  N15: IC2.CE, 74HC139N1.1Y0
  N16: IC3.CS2, 74HC139N1.1Y1

custom parts:
  Z80 A: Zilog Z80 A CPU
  W27C512: Winbond 64K x 8 EEPROM
  628128: 128K x 8 SRAM
