# Fritzing sketch Z80 Breadboard Computer #3.1 (saved by Fritzing 0.9.4)
breadboards: 3

parts:
  IC1 = Z80 A [package="DIP (Dual Inline) [THT]"]
  C1 = Ceramic Capacitor [capacitance=0.1µF package="100 mil [THT, multilayer]"]
  S1 = Pushbutton [package="[THT]"]
  R17 = Resistor [tolerance=±5% resistance=470 package=THT]
  C2 = Ceramic Capacitor [capacitance=10nF package="100 mil [THT, multilayer]"]
  R19 = Resistor [tolerance=±5% resistance=470 package=THT]
  U1 = 555 Timer [package="DIP8 [THT]"]
  R18 = Rotary Potentiometer (Small) [maximum_resistance=10kΩ package=THT]
  C3 = Electrolytic Capacitor [capacitance=1µF package="100 mil [THT, electrolytic]"]
  C4 = Electrolytic Capacitor [capacitance=10µF package="100 mil [THT, electrolytic]"]
  IC2 = W27C512 [package="DIP (Dual Inline) [THT]"]
  C5 = Ceramic Capacitor [capacitance=0.1µF package="100 mil [THT, multilayer]"]
  IC3 = 628128 [package="DIP (Dual Inline) [THT]"]
  C6 = Ceramic Capacitor [capacitance=0.1µF package="100 mil [THT, multilayer]"]
  74HC139N1 = 74HC139N [part_number=74HC139N package="DIP (Dual Inline) [THT]"]
  Part1 = BluePill
  LCD1 = LCD screen
  R20 = Rotary Potentiometer (Small) [maximum_resistance=10kΩ package=THT]

nets:
  A11: IC1.A11, IC2.A11, IC3.A11
  A12: IC1.A12, IC2.A12, IC3.A12
  A13: IC1.A13, IC2.A13, IC3.A13
  A14: IC1.A14, IC2.A14, IC3.A14
  A15: IC1.A15, IC2.A15, IC3.A15, 74HC139N1.1A
  CLOCK: IC1.CLK, U1.Output
  D4: IC1.D4, IC2.Q4, IC3.D4, Part1.B4
  D3: IC1.D3, IC2.Q3, IC3.D3, Part1.B6
  D5: IC1.D5, IC2.Q5, IC3.D5, Part1.B3
  D6: IC1.D6, IC2.Q6, IC3.D6, Part1.A15
  5V: IC1.+5V, IC1.!_INT, IC1.!_NMI, IC1.!_WAIT, IC1.!_BUSRQ, C1.1, R17.Pin_0, R19.Pin_1, U1.Reset, U1.Vcc_Supply_Voltage, C4.+, IC2.Vcc, C5.1, IC3.CS2, IC3.Vcc, C6.1, 74HC139N1.VCC, Part1.5V, LCD1.VDD, LCD1.LED+, R20.leg2
  D2: IC1.D2, IC2.Q2, IC3.D2, Part1.B7
  D7: IC1.D7, IC2.Q7, IC3.D7, Part1.A10
  D0: IC1.D0, IC2.Q0, IC3.D0, Part1.B9
  D1: IC1.D1, IC2.Q1, IC3.D1, Part1.B8
  MREQ: IC1.!_MREQ, 74HC139N1.1G_
  IORQ: IC1.!_IRQ, Part1.B12
  RD: IC1.!_RD, IC2.OE/Vpp, IC3.OE, Part1.B14
  WR: IC1.!_WR, IC3.WE, Part1.B13
  N1: IC1.!_RESET, S1.Pin_3, S1.Pin_4, R17.Pin_1
  GND: IC1.GND, C1.0, S1.Pin_1, S1.Pin_2, C2.1, U1.Ground, C3.-, C4.-, IC2.GND, C5.0, IC3.A16, IC3.Vss, C6.0, 74HC139N1.1B, 74HC139N1.GND, 74HC139N1.2G_, Part1.GND3, LCD1.VSS, LCD1.R/W, LCD1.LED-, R20.leg1
  A0: IC1.A0, IC2.A0, IC3.A0, Part1.A9
  A1: IC1.A1, IC2.A1, IC3.A1, Part1.A8
  A2: IC1.A2, IC2.A2, IC3.A2, Part1.B15
  A3: IC1.A3, IC2.A3, IC3.A3
  A4: IC1.A4, IC2.A4, IC3.A4
  A5: IC1.A5, IC2.A5, IC3.A5
  A6: IC1.A6, IC2.A6, IC3.A6
  A7: IC1.A7, IC2.A7, IC3.A7
  A8: IC1.A8, IC2.A8, IC3.A8
  A9: IC1.A9, IC2.A9, IC3.A9
  A10: IC1.A10, IC2.A10, IC3.A10
  N2: C2.0, U1.Control_Voltage
  N3: R19.Pin_0, U1.Discharge, R18.leg2
  N4: U1.Trigger, U1.Threshold, R18.wiper, C3.+
  N5: IC2.CE, 74HC139N1.1Y0
  N6: IC3.CS1, 74HC139N1.1Y1
  N7: Part1.A0, LCD1.DB7
  N8: Part1.A1, LCD1.DB6
  N9: Part1.A3, LCD1.DB4
  N10: Part1.A4, LCD1.DB3
  N11: Part1.A5, LCD1.DB2
  N12: Part1.A6, LCD1.DB1
  N13: Part1.A7, LCD1.DB0
  N14: Part1.B0, LCD1.E
  N15: Part1.B1, LCD1.RS
  N16: Part1.A2, LCD1.DB5
  N17: LCD1.V0, R20.wiper

custom parts:
  Z80 A: Zilog Z80 A CPU
  W27C512: Winbond 64K x 8 EEPROM
  628128: 128K x 8 SRAM
