# Fritzing sketch Z80 Breadboard Computer #4.3 (saved by Fritzing 0.9.4)
breadboards: 4

parts:
  IC1 = Z80 A [package="DIP (Dual Inline) [THT]"]
  C1 = Ceramic Capacitor [capacitance=0.1µF package="100 mil [THT, multilayer]"]
  S1 = Pushbutton [package="[THT]"]
  R17 = Resistor [tolerance=±5% resistance=470 package=THT]
  C2 = Ceramic Capacitor [capacitance=10nF package="100 mil [THT, multilayer]"]
  R19 = Resistor [tolerance=±5% resistance=470 package=THT]
  U1 = 555 Timer [package="DIP8 [THT]"]
  R18 = Rotary Potentiometer (Small) [maximum_resistance=10kΩ package=THT]
  C3 = Electrolytic Capacitor [capacitance=1µF package="100 mil [THT, electrolytic]"]
  C4 = Electrolytic Capacitor [capacitance=10µF package="100 mil [THT, electrolytic]"]
  IC2 = W27C512 [package="DIP (Dual Inline) [THT]"]
  C5 = Ceramic Capacitor [capacitance=0.1µF package="100 mil [THT, multilayer]"]
  IC3 = 628128 [package="DIP (Dual Inline) [THT]"]
  C6 = Ceramic Capacitor [capacitance=0.1µF package="100 mil [THT, multilayer]"]
  Part1 = BluePill
  LCD1 = LCD screen
  R20 = Rotary Potentiometer (Small) [maximum_resistance=10kΩ package=THT]
  microSD1 = MicroSD Card Module
  IC5 = IC, DIP package, 40 pins [chip_label=82C50A]
  U2 = OSCILLATOR [package=crystal-osc-smd-5x3]
  IC4 = DIP - 24 pins [chip_label=ATF22V10C package="DIP (Dual Inline) [THT]"]

nets:
  A11: IC1.A11, IC2.A11, IC3.A11
  A12: IC1.A12, IC2.A12, IC3.A12
  A13: IC1.A13, IC2.A13, IC3.A13
  A14: IC1.A14, IC2.A14, IC3.A14, IC4.A14
  A15: IC1.A15, IC2.A15, IC3.A15, IC4.A15
  CLOCK: IC1.CLK, U1.Output
  D4: IC1.D4, IC2.Q4, IC3.D4, Part1.B12, IC5.pin5
  D3: IC1.D3, IC2.Q3, IC3.D3, Part1.B9, IC5.pin4
  D5: IC1.D5, IC2.Q5, IC3.D5, Part1.B13, IC5.pin6
  D6: IC1.D6, IC2.Q6, IC3.D6, Part1.B14, IC5.pin7
  5V: IC1.+5V, IC1.!_INT, IC1.!_NMI, IC1.!_WAIT, IC1.!_BUSRQ, C1.1, R17.Pin_0, R19.Pin_1, U1.Reset, U1.Vcc_Supply_Voltage, C4.+, IC2.Vcc, C5.1, IC3.CS2, IC3.Vcc, C6.1, Part1.5V, LCD1.VDD, LCD1.LED+, R20.leg2, microSD1.VCC, IC5.pin12, IC5.pin13, IC5.pin40, U2.VCC, IC4.VCC
  D2: IC1.D2, IC2.Q2, IC3.D2, Part1.B8, IC5.pin3
  D7: IC1.D7, IC2.Q7, IC3.D7, Part1.B15, IC5.pin8
  D0: IC1.D0, IC2.Q0, IC3.D0, Part1.B6, IC5.pin1
  D1: IC1.D1, IC2.Q1, IC3.D1, Part1.B7, IC5.pin2
  MREQ: IC1.!_MREQ, IC4.MREQ
  IORQ: IC1.!_IRQ, IC4.IOREQ
  RD: IC1.!_RD, IC2.OE/Vpp, IC3.OE, Part1.B4, IC5.pin21
  WR: IC1.!_WR, IC3.WE, Part1.B3, IC5.pin18
  N1: IC1.!_RESET, S1.Pin_3, S1.Pin_4, R17.Pin_1
  GND: IC1.GND, C1.0, S1.Pin_1, S1.Pin_2, C2.1, U1.Ground, C3.-, C4.-, IC2.GND, C5.0, IC3.A16, IC3.Vss, C6.0, Part1.GND3, LCD1.VSS, LCD1.R/W, LCD1.LED-, R20.leg1, microSD1.GND, IC5.pin19, IC5.pin20, IC5.pin22, IC5.pin25, U2.GND, IC4.GND
  A0: IC1.A0, IC2.A0, IC3.A0, Part1.A8, IC5.pin28
  A1: IC1.A1, IC2.A1, IC3.A1, Part1.A9, IC5.pin27, IC4.A1
  A2: IC1.A2, IC2.A2, IC3.A2, Part1.A10, IC5.pin26, IC4.A2
  A3: IC1.A3, IC2.A3, IC3.A3, IC4.A3
  A4: IC1.A4, IC2.A4, IC3.A4, IC4.A4
  A5: IC1.A5, IC2.A5, IC3.A5, IC4.A5
  A6: IC1.A6, IC2.A6, IC3.A6, IC4.A6
  A7: IC1.A7, IC2.A7, IC3.A7, IC4.A7
  A8: IC1.A8, IC2.A8, IC3.A8
  A9: IC1.A9, IC2.A9, IC3.A9
  A10: IC1.A10, IC2.A10, IC3.A10
  N2: C2.0, U1.Control_Voltage
  N3: R19.Pin_0, U1.Discharge, R18.leg2
  N4: U1.Trigger, U1.Threshold, R18.wiper, C3.+
  CSROM: IC2.CE, IC4.ROMCS
  CSRAM: IC3.CS1, IC4.RAMCS
  N5: Part1.A0, LCD1.DB7
  N6: Part1.A1, LCD1.DB6
  N7: Part1.A3, LCD1.DB4
  PA5: Part1.A5, microSD1.SCK
  PA6: Part1.A6, microSD1.MISO
  PA7: Part1.A7, microSD1.MOSI
  N8: Part1.B0, LCD1.E
  RX: Part1.B10, IC5.pin10
  TX: Part1.B11, IC5.pin11
  N9: Part1.A15, IC4.NC#22
  N10: Part1.B1, LCD1.RS
  N11: Part1.A2, LCD1.DB5
  N12: LCD1.V0, R20.wiper
  N13: IC5.pin9, IC5.pin15
  CSUART: IC5.pin14, IC4.NC#15
  N14: IC5.pin16, U2.OUT
  MR: IC5.pin35

custom parts:
  Z80 A: Zilog Z80 A CPU
  W27C512: Winbond 64K x 8 EEPROM
  628128: 128K x 8 SRAM
  DIP - 24 pins: A DIP stand-in part for whatever IC you want. With 24 pins on a 300mil dual inline package (DIP) footprint.
